# Fritzing sketch hexSchmittTrigger (saved by Fritzing 0.9.9b)
breadboards: 1

parts:
  IC1 = Hex Inverter Schmitt Trigger SN74HC14 [package="DIP (Dual Inline)"]
  R1 = Resistor [tolerance=±5% resistance=120k package="0402 [SMD]"]
  D1 = Diode [package=diode-1n4001]
  C2 = Capacitor [part_number=104 package=cap-pth-small2]
  S4 = Pushbutton [package=THT]
  SP1 = SPEAKER [package=pcb_mount_speaker]
  X1 = USB Connectors [package=usb-b-pth-vertical]
  D2 = Diode [package=diode-1n4001]
  S5 = Pushbutton [package=THT]
  C3 = Capacitor [part_number=104 package=cap-pth-small2]
  R2 = Resistor [tolerance=±5% resistance=100k package="0402 [SMD]"]

nets:
  N1: IC1.1A, R1.Pin_1, S4.leg1
  N2: IC1.1Y, R1.Pin_0, D1.A
  N3: IC1.2A, S5.leg1, R2.Pin_1
  N4: IC1.2Y, D2.A, R2.Pin_0
  GND: IC1.GND, C2.2, SP1.-, X1.GND, C3.2
  5V: IC1.VCC, X1.VBUS
  N5: D1.C, SP1.+, D2.C
  N6: C2.1, S4.leg0
  N7: S5.leg0, C3.1

notes:
  resistor controls Frequency, try values around 100K and try a pot or LDR in series
  for smoother 'mixing' use a resistors instead. With diodes the signals interfere with each other
  Repeat this circuit for the 4 other pairs of input and output pins to get 6 oscillators
  I'm actually using a 4584 hex schmitt trigger inverter, but should work the same with this chip
