# Fritzing sketch solenoidCircuit (saved by Fritzing 0.9.6b)
breadboards: 1

parts:
  Q1 = MOSFET-NCHANNEL [package=to220v]
  Part1 = Arduino Micro (Rev3)  # not connected
  R1 = Resistor [tolerance=±5% resistance=1k package="0805 [SMD]"]
  L1 = Solenoid
  VCC1 = Battery block 9V

nets:
  N1: Q1.G, R1.Pin_0
  N2: Q1.D, L1.pin1
  N3: Q1.S, R1.Pin_1, VCC1.-

notes:
  IRF520 MOSFET transistor
